# Fritzing sketch Filament Scale Sketch (saved by Fritzing 0.9.3b)

parts:
  HUZZAH32 = Adafruit HUZZAH32 ESP32 Feather [part_number="Adafruit #3405"]
  DHT22 = DHT22 Humidity and Temperature Sensor
  Part2 = TFT 1.8 inch 160x128 w microSD [part_number=358]
  HX711 = HX711 Weighing Sensor Module
  R1 = Resistor [tolerance=±5% resistance=10k package=THT]
  Front_Pushbutton = Momentary Switch [package=ksa_sealed_tac_switch]
  Rear_Rocker_Switch_-_On/Off = Taiway 100-SP-X-T1 SPDT Miniature Toggle Switch [part_number=100-SP-X-T1-0-0-B1-M1 package=THT]
  RE1 = KY-040 Rotary encoder [package=THT]

nets:
  N1: HUZZAH32.IO21, Part2.CARDCS
  N2: HUZZAH32.MISO, Part2.MISO
  N3: HUZZAH32.MOSI, Part2.MOSI
  N4: HUZZAH32.SCK, Part2.SCLK
  N5: HUZZAH32.A5_IO4, HX711.CK/TX
  N6: HUZZAH32.A4_IO36, RE1.CLK
  N7: HUZZAH32.A3_I39, RE1.DT
  N8: HUZZAH32.A2_I34, HX711.DO/RX
  N9: HUZZAH32.A1_DAC1, Front_Pushbutton.1
  N10: HUZZAH32.A0_DAC2, Part2.LITE
  N11: HUZZAH32.EN, Rear_Rocker_Switch_-_On/Off.L2
  N12: HUZZAH32.IO13_A12, RE1.SW
  N13: HUZZAH32.IO27_A10, DHT22.DATA, R1.Pin_1
  N14: HUZZAH32.IO15_A8, Part2.RESET
  N15: HUZZAH32.IO32_A7, Part2.TFTDC
  N16: HUZZAH32.IO14_A6, Part2.TFTCS
  N17: DHT22.VDD, R1.Pin_0
  N18: HX711.GND, Front_Pushbutton.3

notes:
  DHT22
  Rear Rocker Switch
  On / Off
  Front Pushbutton
  HX711
  HUZZAH32
  Gnd
  +
  Encoder
  To Load Cell

custom parts:
  TFT 1.8 inch 160x128 w microSD: This lovely little display breakout is the best way to add a small, colorful and bright display to any project. Since the display uses 4-wire SPI to communicate and has its own pixel-addressable frame buffer, it can be used with every kind of microcontroller. Even a very small one with low memory and few pins available! The 1.8" display has 128x160 color pixels.
  KY-040 Rotary encoder: KY-040 Rotary Encoder with switch on breakout borad from AZ Delivery
